// Logisim project 4-bit look ahead adder.circ as structural Verilog: 1 circuit, main circuit main
module main (
  input  in_1,
  input  in_2,
  input  in_3,
  input  in_4,
  input  in_5,
  input  in_6,
  input  in_7,
  output out_8,
  output out_9,
  output out_10
);

  wire and_1_out, and_2_out, and_3_out, and_4_out, and_5_out, and_6_out;

  and and_1 (and_1_out, in_7, in_5, in_3, in_1);
  and and_2 (and_2_out, in_6, in_3, in_1);
  and and_3 (and_3_out, in_4, in_1);
  and and_4 (and_4_out, in_7, in_5, in_3);
  and and_5 (and_5_out, in_6, in_3);
  and and_6 (and_6_out, in_7, in_5);
  or or_1 (out_8, and_1_out, and_2_out, and_3_out, in_2);
  or or_2 (out_9, and_4_out, and_5_out, in_4);
  or or_3 (out_10, and_6_out, in_6);
endmodule
